// Logisim project 4-bit-register.circ as structural Verilog: 1 circuit, main circuit main
module main (
  input  D_0,
  input  EN,
  input  D_1,
  input  D_2,
  input  D_3,
  output Q_0,
  output Q_prime,
  output Q_1,
  output Q_prime_2,
  output Q_2,
  output Q_prime_3,
  output Q_3,
  output Q_prime_4
);

  wire AND_2_out, AND_3_out, AND_4_out, AND_5_out, AND_6_out, AND_7_out, AND_8_out, AND_out, not_1_out,
       not_2_out, not_3_out, not_4_out;

  not not_1 (not_1_out, D_0);
  not not_2 (not_2_out, D_1);
  not not_3 (not_3_out, D_2);
  not not_4 (not_4_out, D_3);
  and AND (AND_out, not_1_out, EN);
  and AND_2 (AND_2_out, EN, D_0);
  and AND_3 (AND_3_out, not_2_out, EN);
  and AND_4 (AND_4_out, EN, D_1);
  and AND_5 (AND_5_out, not_3_out, EN);
  and AND_6 (AND_6_out, EN, D_2);
  and AND_7 (AND_7_out, not_4_out, EN);
  and AND_8 (AND_8_out, EN, D_3);
  nor nor_1 (Q_0, AND_out, Q_prime);
  nor nor_2 (Q_prime, Q_0, AND_2_out);
  nor nor_3 (Q_1, AND_3_out, Q_prime_2);
  nor nor_4 (Q_prime_2, Q_1, AND_4_out);
  nor nor_5 (Q_2, AND_5_out, Q_prime_3);
  nor nor_6 (Q_prime_3, Q_2, AND_6_out);
  nor nor_7 (Q_3, AND_7_out, Q_prime_4);
  nor nor_8 (Q_prime_4, Q_3, AND_8_out);

  // Notes on the sheet:
  //   4-Bit Register
  //   EN->Q=D
  //   EN
  //   EN
  //   EN
  //   R
  //   S
  //   R
  //   S
  //   R
  //   S
  //   R
  //   S
  //   S-R Latch
endmodule
