// Logisim project ALU.circ as structural Verilog: 1 circuit, main circuit main
module main (
  input  [3:0] in_1,
  input  [3:0] in_2,
  input  [1:0] in_3,
  output [3:0] out_4
);

  wire adder_1_cout, adder_2_cout, adder_3_cout, subtractor_1_bout, subtractor_2_bout, subtractor_3_bout;
  wire [1:0] undriven;
  wire [3:0] adder_1_out, and_1_out, or_1_out, subtractor_1_out;

  Adder #(.width(1)) adder_1 (.a(in_1[0]), .b(in_2[0]), .out(adder_1_out[0]), .cout(adder_1_cout));  // open: cin
  Adder #(.width(1)) adder_2 (.a(in_1[1]), .b(in_2[1]), .out(adder_1_out[1]), .cin(adder_1_cout), .cout(adder_2_cout));
  Adder #(.width(1)) adder_3 (.a(in_1[2]), .b(in_2[2]), .out(adder_1_out[2]), .cin(adder_2_cout), .cout(adder_3_cout));
  Adder #(.width(1)) adder_4 (.a(in_1[3]), .b(in_2[3]), .out(adder_1_out[3]), .cin(adder_3_cout));  // open: cout
  Subtractor #(.width(1)) subtractor_1 (
    .a(in_1[0]), .b(in_2[0]), .out(subtractor_1_out[0]), .bout(subtractor_1_bout));  // open: bin
  Subtractor #(.width(1)) subtractor_2 (
    .a(in_1[1]), .b(in_2[1]), .out(subtractor_1_out[1]), .bin(subtractor_1_bout), .bout(subtractor_2_bout));
  Subtractor #(.width(1)) subtractor_3 (
    .a(in_1[2]), .b(in_2[2]), .out(subtractor_1_out[2]), .bin(subtractor_2_bout), .bout(subtractor_3_bout));
  Subtractor #(.width(1)) subtractor_4 (
    .a(in_1[3]), .b(in_2[3]), .out(subtractor_1_out[3]), .bin(subtractor_3_bout));  // open: bout
  and and_1 (and_1_out[0], in_1[0], in_2[0]);
  and and_2 (and_1_out[1], in_1[1], in_2[1]);
  and and_3 (and_1_out[2], in_1[2], in_2[2]);
  and and_4 (and_1_out[3], in_1[3], in_2[3]);
  or or_1 (or_1_out[0], in_1[0], in_2[0]);
  or or_2 (or_1_out[1], in_1[1], in_2[1]);
  or or_3 (or_1_out[2], in_1[2], in_2[2]);
  or or_4 (or_1_out[3], in_1[3], in_2[3]);
  Multiplexer #(.select(2), .width(4), .disabled(0), .enable("false")) multiplexer_1 (
    .in0(adder_1_out), .in1(subtractor_1_out), .in2(and_1_out), .in3(or_1_out), .out(out_4), .sel(undriven));
endmodule
