// Logisim project ALU_with_Registers.circ as structural Verilog: 1 circuit, main circuit main
module main (
  input  D_0,
  input  EN,
  input  D_1,
  input  D_2,
  input  D_3,
  input  [1:0] in_6,
  input  D_0_2,
  input  EN_2,
  input  D_1_2,
  input  D_2_2,
  input  D_3_2,
  output Q_prime,
  output Q_prime_2,
  output Q_prime_3,
  output [3:0] out_15,
  output Q_prime_4,
  output Q_prime_5,
  output Q_prime_6,
  output Q_prime_7,
  output Q_prime_8
);

  wire AND_2_out, AND_3_out, AND_4_out, AND_5_out, AND_6_out, AND_7_out, AND_8_out, AND_9_out, AND_10_out,
       AND_11_out, AND_12_out, AND_13_out, AND_14_out, AND_15_out, AND_17_out, AND_out, not_1_out, not_2_out,
       not_3_out, not_4_out, not_5_out, not_6_out, not_7_out, not_8_out;
  wire [1:0] undriven;
  wire [3:0] adder_1_out, and_18_out, nor_1_out, nor_9_out, or_1_out, subtractor_1_out;

  not not_1 (not_1_out, D_0);
  not not_2 (not_2_out, D_1);
  not not_3 (not_3_out, D_2);
  not not_4 (not_4_out, D_3);
  not not_5 (not_5_out, D_0_2);
  not not_6 (not_6_out, D_1_2);
  not not_7 (not_7_out, D_2_2);
  not not_8 (not_8_out, D_3_2);
  and AND (AND_out, not_1_out, EN);
  and AND_2 (AND_2_out, EN, D_0);
  and AND_3 (AND_3_out, not_2_out, EN);
  and AND_4 (AND_4_out, EN, D_1);
  and AND_5 (AND_5_out, not_3_out, EN);
  and AND_6 (AND_6_out, EN, D_2);
  and AND_7 (AND_7_out, not_4_out, EN);
  and AND_8 (AND_8_out, EN, D_3);
  and AND_9 (AND_9_out, not_5_out, EN_2);
  and AND_10 (AND_10_out, EN_2, D_0_2);
  and AND_11 (AND_11_out, not_6_out, EN_2);
  and AND_12 (AND_12_out, EN_2, D_1_2);
  and AND_13 (AND_13_out, not_7_out, EN_2);
  and AND_14 (AND_14_out, EN_2, D_2_2);
  and AND_15 (AND_15_out, not_8_out, EN_2);
  // AND_Gate AND_16 is placed but not wired
  and AND_17 (AND_17_out, EN_2, D_3_2);
  nor nor_1 (nor_1_out[0], AND_out, Q_prime);
  nor nor_2 (Q_prime, nor_1_out[0], AND_2_out);
  nor nor_3 (nor_1_out[1], AND_3_out, Q_prime_2);
  nor nor_4 (Q_prime_2, nor_1_out[1], AND_4_out);
  nor nor_5 (nor_1_out[2], AND_5_out, Q_prime_3);
  nor nor_6 (Q_prime_3, nor_1_out[2], AND_6_out);
  nor nor_7 (nor_1_out[3], AND_7_out, Q_prime_4);
  nor nor_8 (Q_prime_4, nor_1_out[3], AND_8_out);
  nor nor_9 (nor_9_out[0], AND_9_out, Q_prime_5);
  nor nor_10 (Q_prime_5, nor_9_out[0], AND_10_out);
  nor nor_11 (nor_9_out[1], AND_11_out, Q_prime_6);
  nor nor_12 (Q_prime_6, nor_9_out[1], AND_12_out);
  nor nor_13 (nor_9_out[2], AND_13_out, Q_prime_7);
  nor nor_14 (Q_prime_7, nor_9_out[2], AND_14_out);
  nor nor_15 (nor_9_out[3], AND_15_out, Q_prime_8);
  nor nor_16 (Q_prime_8, nor_9_out[3], AND_17_out);
  DotMatrix #(.matrixcols(1), .matrixrows(4)) dotmatrix_1 (.col0(nor_1_out));
  DotMatrix #(.matrixcols(1), .matrixrows(4)) dotmatrix_2 (.col0(nor_9_out));
  Adder #(.width(4)) adder_1 (.a(nor_1_out), .b(nor_9_out), .out(adder_1_out));  // open: cin, cout
  Subtractor #(.width(4)) subtractor_1 (.a(nor_1_out), .b(nor_9_out), .out(subtractor_1_out));  // open: bin, bout
  assign and_18_out = nor_1_out & nor_9_out;  // AND_Gate and_18, 4 bits wide
  assign or_1_out = nor_1_out | nor_9_out;  // OR_Gate or_1, 4 bits wide
  Multiplexer #(.select(2), .width(4), .enable("false")) multiplexer_1 (
    .in0(adder_1_out), .in1(subtractor_1_out), .in2(and_18_out), .in3(or_1_out), .out(out_15), .sel(undriven));

  // Notes on the sheet:
  //   Register 1
  //   EN->Q=D
  //   EN
  //   Register 2
  //   EN->Q=D
  //   EN
  //   EN
  //   EN
  //   EN
  //   EN
  //   R
  //   S
  //   R
  //   S
  //   R
  //   S
  //   R
  //   S
  //   R
  //   S
  //   R
  //   S
  //   R
  //   S
  //   R
  //   S
  //   S-R Latch
  //   Q[0]
  //   Q[1]
  //   Q[2]
  //   Q[3]
  //   Q[0]
  //   Q[1]
  //   Q[2]
  //   Q[3]
endmodule
