// Logisim project FullAdder.circ as structural Verilog: 1 circuit, main circuit main
module main (
  input  A0,
  input  B0,
  input  C0,
  input  D0,
  input  A1,
  input  B1,
  input  C1,
  input  D1,
  input  in_9,
  input  in_10,
  output s0,
  output out_1,
  output s2,
  output S3,
  output c3,
  output out_16
);

  wire and_1_out, and_3_out, and_4_out, and_5_out, and_6_out, and_7_out, and_8_out, nand_1_out, or_1_out,
       or_2_out, or_3_out, xor_2_out, xor_4_out, xor_6_out;

  xor xor_1 (s0, A0, A1);
  and and_1 (and_1_out, A0, A1);
  nand nand_1 (nand_1_out, in_9, in_10);
  or or_1 (or_1_out, in_9, in_10);
  and and_2 (out_16, nand_1_out, or_1_out);
  xor xor_2 (xor_2_out, B0, B1);
  and and_3 (and_3_out, B0, B1);
  xor xor_3 (out_1, xor_2_out, and_1_out);
  and and_4 (and_4_out, xor_2_out, and_1_out);
  or or_2 (or_2_out, and_4_out, and_3_out);
  xor xor_4 (xor_4_out, C0, C1);
  and and_5 (and_5_out, C0, C1);
  xor xor_5 (s2, or_2_out, xor_4_out);
  and and_6 (and_6_out, or_2_out, xor_4_out);
  or or_3 (or_3_out, and_6_out, and_5_out);
  xor xor_6 (xor_6_out, D0, D1);
  and and_7 (and_7_out, D0, D1);
  xor xor_7 (S3, or_3_out, xor_6_out);
  and and_8 (and_8_out, or_3_out, xor_6_out);
  or or_4 (c3, and_8_out, and_7_out);

  // Notes on the sheet:
  //   Adder
  //   Xor Implementation:
  //   A0
  //   A1
  //   A0
  //   A1
  //   out0
  //   c0
  //   B0
  //   B1
  //   B0
  //   B1
  //   s1
  //   c1
  //   C0
  //   C1
  //   C0
  //   C1
  //   out[2]
  //   c2
  //   D0
  //   D1
  //   D0
  //   D1
  //   out[3]
  //   out[4]
  //   1IF overflow
endmodule
