// Logisim project Subtractor.circ as structural Verilog: 1 circuit, main circuit main
module main (
  input  A0,
  input  B0,
  input  C0,
  input  D0,
  input  A1,
  input  B1,
  input  C1,
  input  D1,
  output s0,
  output s1,
  output s2,
  output S3,
  output c3,
  output c3_2
);

  wire and_1_out, and_2_out, and_3_out, and_5_out, and_6_out, and_7_out, and_8_out, and_9_out, and_10_out,
       and_11_out, not_1_out, not_2_out, not_3_out, not_4_out, or_1_out, or_2_out, xor_1_out, xor_2_out,
       xor_3_out, xor_4_out, xor_6_out, xor_8_out, xor_10_out;

  not not_1 (not_1_out, A1);
  not not_2 (not_2_out, B1);
  not not_3 (not_3_out, C1);
  not not_4 (not_4_out, D1);
  xor xor_1 (xor_1_out, not_1_out, 1'b1);
  and and_1 (and_1_out, not_1_out, 1'b1);
  xor xor_2 (xor_2_out, and_1_out, not_2_out);
  and and_2 (and_2_out, and_1_out, not_2_out);
  xor xor_3 (xor_3_out, and_2_out, not_3_out);
  and and_3 (and_3_out, and_2_out, not_3_out);
  xor xor_4 (xor_4_out, and_3_out, not_4_out);
  and and_4 (c3_2, and_3_out, not_4_out);
  xor xor_5 (s0, A0, xor_1_out);
  and and_5 (and_5_out, A0, xor_1_out);
  xor xor_6 (xor_6_out, B0, xor_2_out);
  and and_6 (and_6_out, B0, xor_2_out);
  xor xor_7 (s1, and_5_out, xor_6_out);
  and and_7 (and_7_out, and_5_out, xor_6_out);
  or or_1 (or_1_out, and_7_out, and_6_out);
  xor xor_8 (xor_8_out, C0, xor_3_out);
  and and_8 (and_8_out, C0, xor_3_out);
  and and_9 (and_9_out, or_1_out, xor_8_out);
  xor xor_9 (s2, or_1_out, xor_8_out);
  or or_2 (or_2_out, and_8_out, and_9_out);
  xor xor_10 (xor_10_out, D0, xor_4_out);
  and and_10 (and_10_out, D0, xor_4_out);
  xor xor_11 (S3, or_2_out, xor_10_out);
  and and_11 (and_11_out, or_2_out, xor_10_out);
  or or_3 (c3, and_11_out, and_10_out);

  // Notes on the sheet:
  //   A1
  //   1
  //   A1
  //   1
  //   *Multiplexor Implementation shown in the Adder gate*
  //   s0
  //   c0
  //   c0
  //   s1
  //   B1
  //   c0
  //   c1
  //   B1
  //   s2
  //   c2
  //   s3
  //   2's complement converter gate
  //   Ignored
  //   A0
  //   A1
  //   A0
  //   A1
  //   c0
  //   B0
  //   B1
  //   B0
  //   B1
  //   c1
  //   C0
  //   C1
  //   C0
  //   C1
  //   c2
  //   D0
  //   D1
  //   D0
  //   D1
  //   1IF overflow
endmodule
